// Logisim project lab2.circ as structural Verilog: 2 circuits, main circuit main
module main (
  input  A,
  input  B,
  input  C,
  input  A1,
  input  B1,
  input  C1,
  input  D1,
  output Out1,
  output Out2
);

  wire and_1_out, and_2_out, and_3_out, and_4_out, and_6_out, and_7_out;

  and and_1 (and_1_out, ~A, ~C, B);  // AND_Gate
  and and_2 (and_2_out, ~B, A, ~C);  // AND_Gate
  and and_3 (and_3_out, A, B, C);
  and and_4 (and_4_out, ~A1, ~B1, ~D1, C1);  // AND_Gate
  and and_5 (and_4_out, ~A1, B1, C1, D1);  // AND_Gate
  and and_6 (and_6_out, A1, ~B1, C1, ~D1);  // AND_Gate
  and and_7 (and_7_out, A1, B1, C1, ~D1);  // AND_Gate
  or or_1 (Out1, and_1_out, and_2_out, and_3_out);
  or or_2 (Out2, and_4_out, and_4_out, and_6_out, and_7_out);
endmodule

module equation_1 (
  input  in_1,
  input  in_2,
  input  in_3,
  input  in_4,
  input  in_5,
  input  in_6,
  input  in_7,
  output out_8,
  output out_9
);

  main main_1 (.A(in_1), .B(in_2), .C(in_3), .A1(in_4), .B1(in_5), .C1(in_6), .D1(in_7), .Out1(out_8), .Out2(out_9));
endmodule
