// Logisim project lab3.circ as structural Verilog: 2 circuits, main circuit main
module main (
  input  in1,
  input  in2,
  input  in3,
  input  in4,
  input  in5,
  input  in6,
  input  in7,
  input  in8,
  input  in9,
  output out1,
  output out2,
  output out3,
  output out4
);

  wire and_1_out, u1_out, u2_out, u3_out, u4_out, u5_out, u6_out, u7_out, u9_out, u10_out, u11_out, u12_out,
       u16_out, undriven;

  nor u16 (u16_out, in8, in9);
  and u1 (u1_out, in1, ~in2, ~in4, ~in6, u16_out);  // AND_Gate
  and u2 (u2_out, in3, ~in4, ~in6, u16_out);  // AND_Gate
  and u3 (u3_out, in5, ~in6, u16_out);  // AND_Gate
  and u4 (u4_out, in7, u16_out);
  and u5 (u5_out, in2, ~in4, ~in5, u16_out);  // AND_Gate
  and u6 (u6_out, ~in4, ~in5, in3, u16_out);  // AND_Gate
  and u7 (u7_out, in6, u16_out);
  and and_1 (and_1_out, undriven, u16_out);
  and u8 (and_1_out, undriven, u16_out);
  and u9 (u9_out, in4, u16_out);
  and u10 (u10_out, in5, u16_out);
  and u11 (u11_out, in6, u16_out);
  and u12 (u12_out, in7, u16_out);
  or u13 (out1, u1_out, u2_out, u3_out, u4_out, in9);
  or u14 (out2, u5_out, u6_out, u7_out, and_1_out);
  or u15 (out3, u9_out, u10_out, u11_out, u12_out);
  or u17 (out4, in9, in8);
endmodule

module encoder (
  input  in_1,
  input  in_2,
  input  in_3,
  input  in_4,
  input  in_5,
  input  in_6,
  input  in_7,
  input  in_8,
  input  in_9,
  output [3:0] out_10
);

  main main_1 (
    .in1(in_1), .in2(in_2), .in3(in_3), .in4(in_4), .in5(in_5), .in6(in_6), .in7(in_7), .in8(in_8),
    .in9(in_9), .out1(out_10[0]), .out2(out_10[1]), .out3(out_10[2]), .out4(out_10[3]));
  Hex_Digit_Display hex_digit_display_1 (.value(out_10));  // open: dp
endmodule
