// Logisim project lab5.circ as structural Verilog: 6 circuits, main circuit main
module main (
  input  Reset,
  input  clkUniversal,
  input  resetUniversal,
  input  [1:0] selectUniversal,
  output [3:0] out_5
);

  wire clk_out;
  wire [3:0] ring_1_ring;

  Clock #(.highDuration(4), .lowDuration(4)) clk (.out(clk_out));
  Clock sysclk ();  // open: out
  Ring ring_1 (.clk2(clk_out), .rst2(Reset), .ring(ring_1_ring));
  // Probe on ring_1_ring
  Hex_Digit_Display hex_digit_display_1 (.value(ring_1_ring));  // open: dp
  Universal universal_1 (.clk(clkUniversal), .reset(resetUniversal), .Sel(selectUniversal), .CountOut(out_5));

  // Notes on the sheet:
  //   Select Counter: 0 - Up, 1 - Down, 2 - Ring, 3 - Johnson
endmodule

module Up (
  input  clk0,
  input  rst0,
  output [3:0] up
);

  wire d_ff_1_qn, d_ff_2_qn, d_ff_3_qn, d_ff_4_qn;

  D_Flip_Flop d_ff_1 (.D(d_ff_1_qn), .clk(clk0), .Q(up[0]), .Qn(d_ff_1_qn), .reset(rst0));  // open: preset
  D_Flip_Flop d_ff_2 (.D(d_ff_2_qn), .clk(d_ff_1_qn), .Q(up[1]), .Qn(d_ff_2_qn), .reset(rst0));  // open: preset
  D_Flip_Flop d_ff_3 (.D(d_ff_3_qn), .clk(d_ff_2_qn), .Q(up[2]), .Qn(d_ff_3_qn), .reset(rst0));  // open: preset
  D_Flip_Flop d_ff_4 (.D(d_ff_4_qn), .clk(d_ff_3_qn), .Q(up[3]), .Qn(d_ff_4_qn), .reset(rst0));  // open: preset
endmodule

module Universal (
  input  clk,
  input  reset,
  input  [1:0] Sel,
  output [3:0] CountOut
);

  wire [3:0] down_1_down, johnson_1_johnson, ring_1_ring, up_1_up;

  Up up_1 (.clk0(clk), .rst0(reset), .up(up_1_up));
  Down down_1 (.rst1(reset), .clk1(clk), .down(down_1_down));
  Ring ring_1 (.clk2(clk), .rst2(reset), .ring(ring_1_ring));
  Johnson johnson_1 (.clk3(clk), .rst3(reset), .johnson(johnson_1_johnson));
  Multiplexer #(.select(2), .width(4)) multiplexer_1 (
    .in0(up_1_up), .in1(down_1_down), .in2(ring_1_ring), .in3(johnson_1_johnson), .out(CountOut), .sel(Sel));
endmodule

module Johnson (
  input  clk3,
  input  rst3,
  output [3:0] johnson
);

  wire d_ff_4_qn;

  D_Flip_Flop d_ff_1 (.D(d_ff_4_qn), .clk(clk3), .Q(johnson[0]), .preset(rst3));  // open: Qn, reset
  D_Flip_Flop d_ff_2 (.D(johnson[0]), .clk(clk3), .Q(johnson[1]), .reset(rst3));  // open: Qn, preset
  D_Flip_Flop d_ff_3 (.D(johnson[1]), .clk(clk3), .Q(johnson[2]), .reset(rst3));  // open: Qn, preset
  D_Flip_Flop d_ff_4 (.D(johnson[2]), .clk(clk3), .Q(johnson[3]), .Qn(d_ff_4_qn), .reset(rst3));  // open: preset
endmodule

module Ring (
  input  clk2,
  input  rst2,
  output [3:0] ring
);

  D_Flip_Flop d_ff_1 (.D(ring[3]), .clk(clk2), .Q(ring[0]), .preset(rst2));  // open: Qn, reset
  D_Flip_Flop d_ff_2 (.D(ring[0]), .clk(clk2), .Q(ring[1]), .reset(rst2));  // open: Qn, preset
  D_Flip_Flop d_ff_3 (.D(ring[1]), .clk(clk2), .Q(ring[2]), .reset(rst2));  // open: Qn, preset
  D_Flip_Flop d_ff_4 (.D(ring[2]), .clk(clk2), .Q(ring[3]), .reset(rst2));  // open: Qn, preset
endmodule

module Down (
  input  rst1,
  input  clk1,
  output [3:0] down
);

  wire d_ff_1_qn, d_ff_2_qn, d_ff_3_qn, d_ff_4_qn;

  D_Flip_Flop d_ff_1 (.D(d_ff_1_qn), .clk(clk1), .Q(down[0]), .Qn(d_ff_1_qn), .preset(rst1));  // open: reset
  D_Flip_Flop d_ff_2 (.D(d_ff_2_qn), .clk(down[0]), .Q(down[1]), .Qn(d_ff_2_qn), .preset(rst1));  // open: reset
  D_Flip_Flop d_ff_3 (.D(d_ff_3_qn), .clk(down[1]), .Q(down[2]), .Qn(d_ff_3_qn), .preset(rst1));  // open: reset
  D_Flip_Flop d_ff_4 (.D(d_ff_4_qn), .clk(down[2]), .Q(down[3]), .Qn(d_ff_4_qn), .preset(rst1));  // open: reset
endmodule
